# Fritzing sketch Schematic (saved by Fritzing 0.9.9b)
breadboards: 1

parts:
  부품1 = Arduino Leonardo (Rev3b)
  J1 = Basic Force Sensing Resistor (FSR) [package=THT]
  J2 = Basic Force Sensing Resistor (FSR) [package=THT]
  J3 = Basic Force Sensing Resistor (FSR) [package=THT]
  J4 = Basic Force Sensing Resistor (FSR) [package=THT]
  J5 = Basic Force Sensing Resistor (FSR) [package=THT]
  J6 = Basic Force Sensing Resistor (FSR) [package=THT]
  J7 = Basic Force Sensing Resistor (FSR) [package=THT]
  J8 = Basic Force Sensing Resistor (FSR) [package=THT]
  J9 = Basic Force Sensing Resistor (FSR) [package=THT]
  J10 = Basic Force Sensing Resistor (FSR) [package=THT]
  부품2 = Tri-Axis Gyro Breakout - L3G4200D
  U1 = Voltage Regulator - 5V [package="TO220 [THT]"]
  U2 = LIPO-110mAh [package=lipo-110]
  R1 = Resistor [tolerance=±5% power=0.25 resistance=10k package=THT]
  WIZ820io1 = WIZ820io [part_number=WIZ820io]  # not connected

nets:
  N1: 부품1.D2/SDA, 부품1.SDA, 부품2.SDA
  N2: 부품1.D3_PWM/SCL, 부품1.SCL, 부품2.SCL
  N3: 부품1.D4/A6, 부품1.D6_PWM/A7, 부품1.A1, 부품1.A2, 부품1.A3, 부품1.A4, 부품1.A5, 부품1.D8/A8, 부품1.D9_PWM/A9, 부품1.D10_PWM/A10, J1.pin_1, J2.pin_1, J3.pin_1, J4.pin_1, J5.pin_1, J6.pin_1, J7.pin_1, J8.pin_1, J9.pin_1, J10.pin_1, R1.Pin_0
  3V3: 부품1.3V3, 부품2.VCC
  GND: 부품1.GND, U1.GND, U2.-, R1.Pin_1
  N4: 부품1.VIN, J1.pin_0, J2.pin_0, J3.pin_0, J4.pin_0, J5.pin_0, J6.pin_0, J7.pin_0, J8.pin_0, J9.pin_0, J10.pin_0, U1.output_voltage
  N5: U1.input_voltage, U2.+

notes:
  3.7V battery
  step-up module
  3.7V to 5V
  Arduino Pro Micro
  10kOhm
  IMU
  MPU-9250
  Flex Sensor
  Bluetooth module
  HM-11
  RX - TX - GND - VCC
